// Logisim project Dzielenie przez 3.circ as structural Verilog: 2 circuits, main circuit main
module main (
  input  [5:0] in_1,
  output [5:0] out_2
);

  wire podziel3_1_y0_2, podziel3_1_y1_2, podziel3_2_y0_2, podziel3_2_y1_2, podziel3_3_y0_2, podziel3_3_y1_2,
       podziel3_4_y0_2, podziel3_4_y1_2, podziel3_5_y0_2, podziel3_5_y1_2;

  Podziel3 podziel3_1 (.y1(1'b0), .y0(1'b0), .a(in_1[5]), .Y1_2(podziel3_1_y1_2), .Y0_2(podziel3_1_y0_2), .S(out_2[5]));
  Podziel3 podziel3_2 (
    .y1(podziel3_1_y1_2), .y0(podziel3_1_y0_2), .a(in_1[4]), .Y1_2(podziel3_2_y1_2), .Y0_2(podziel3_2_y0_2),
    .S(out_2[4]));
  Podziel3 podziel3_3 (
    .y1(podziel3_2_y1_2), .y0(podziel3_2_y0_2), .a(in_1[3]), .Y1_2(podziel3_3_y1_2), .Y0_2(podziel3_3_y0_2),
    .S(out_2[3]));
  Podziel3 podziel3_4 (
    .y1(podziel3_3_y1_2), .y0(podziel3_3_y0_2), .a(in_1[2]), .Y1_2(podziel3_4_y1_2), .Y0_2(podziel3_4_y0_2),
    .S(out_2[2]));
  Podziel3 podziel3_5 (
    .y1(podziel3_4_y1_2), .y0(podziel3_4_y0_2), .a(in_1[1]), .Y1_2(podziel3_5_y1_2), .Y0_2(podziel3_5_y0_2),
    .S(out_2[1]));
  Podziel3 podziel3_6 (.y1(podziel3_5_y1_2), .y0(podziel3_5_y0_2), .a(in_1[0]), .S(out_2[0]));  // open: Y1_2, Y0_2
endmodule

module Podziel3 (
  input  y1,
  input  y0,
  input  a,
  output Y1_2,
  output Y0_2,
  output S
);

  wire and_1_out, and_2_out, and_3_out, and_4_out, and_5_out, not_1_out, not_2_out, not_3_out, not_4_out;

  not not_1 (not_1_out, a);
  not not_2 (not_2_out, y1);
  not not_3 (not_3_out, y0);
  not not_4 (not_4_out, a);
  and and_1 (and_1_out, y0, a);
  and and_2 (and_2_out, y0, not_1_out);
  and and_3 (and_3_out, y1, a);
  and and_4 (and_4_out, not_2_out, not_3_out, a);
  and and_5 (and_5_out, y1, not_4_out);
  or or_1 (S, and_1_out, y1);
  or or_2 (Y1_2, and_2_out, and_3_out);
  or or_3 (Y0_2, and_4_out, and_5_out);
endmodule
