// Logisim project JK_1.circ as structural Verilog: 1 circuit, main circuit main
module main (
);

  wire and_1_out, and_2_out, clock_1_out, j_k_ff_1_q, j_k_ff_2_q, j_k_ff_2_qn, j_k_ff_3_qn;

  Clock clock_1 (.out(clock_1_out));
  J_K_Flip_Flop j_k_ff_1 (.J(j_k_ff_2_q), .clk(clock_1_out), .K(1'b1), .Q(j_k_ff_1_q));  // open: Qn, preset, en, reset
  and and_1 (and_1_out, j_k_ff_3_qn, j_k_ff_1_q);
  J_K_Flip_Flop j_k_ff_2 (
    .J(1'b1), .clk(clock_1_out), .K(and_1_out), .Q(j_k_ff_2_q), .Qn(j_k_ff_2_qn));  // open: preset, en, reset
  and and_2 (and_2_out, j_k_ff_1_q, j_k_ff_2_q);
  J_K_Flip_Flop j_k_ff_3 (
    .J(j_k_ff_2_qn), .clk(clock_1_out), .K(and_2_out), .Qn(j_k_ff_3_qn));  // open: Q, preset, en, reset

  // Notes on the sheet:
  //   0-->3-->3-->2-->2-->
endmodule
