// Logisim project Przerzutnik JK zbudowany za pomocą T.circ as structural Verilog: 1 circuit, main circuit main
module main (
  input  J,
  input  K
);

  wire and_1_out, and_2_out, clock_1_out, or_1_out, t_ff_1_q, t_ff_1_qn;

  and and_1 (and_1_out, t_ff_1_qn, J);
  and and_2 (and_2_out, K, t_ff_1_q);
  or or_1 (or_1_out, and_1_out, and_2_out);
  Clock clock_1 (.out(clock_1_out));
  T_Flip_Flop t_ff_1 (.clk(clock_1_out), .T(or_1_out), .Q(t_ff_1_q), .Qn(t_ff_1_qn));  // open: preset, reset, en

  // Notes on the sheet:
  //   T = J !Q + K Q
  //   Przerzutnik JK zbudowany za pomocą T
endmodule
