// Logisim project Przerzutniki-zadanie 3.circ as structural Verilog: 1 circuit, main circuit main
module main (
  input  in_1,
  input  in_2,
  input  in_3,
  input  in_4,
  input  in_5,
  input  in_6,
  input  D,
  input  T,
  input  D_2,
  input  J,
  input  J_2,
  input  K,
  input  K_2
);

  wire and_1_out, and_2_out, and_3_out, and_4_out, clock_1_out, clock_2_out, clock_3_out, clock_4_out,
       clock_5_out, clock_6_out, clock_7_out, clock_8_out, clock_9_out, d_ff_1_q, d_ff_1_qn, d_ff_3_q,
       not_1_out, not_2_out, not_3_out, or_1_out, or_2_out, or_3_out, t_ff_2_q, t_ff_3_q, t_ff_3_qn,
       xor_1_out, xor_2_out;

  Clock clock_1 (.out(clock_1_out));
  Clock clock_2 (.out(clock_2_out));
  Clock clock_3 (.out(clock_3_out));
  not not_1 (not_1_out, K);
  T_Flip_Flop t_ff_1 (.clk(clock_1_out), .T(in_1));  // open: Q, Qn, preset, reset, en
  xor xor_1 (xor_1_out, t_ff_2_q, D_2);
  and and_1 (and_1_out, d_ff_1_qn, J);
  and and_2 (and_2_out, not_1_out, d_ff_1_q);
  Clock clock_4 (.out(clock_4_out));
  T_Flip_Flop t_ff_2 (.clk(clock_3_out), .T(xor_1_out), .Q(t_ff_2_q));  // open: Qn, preset, reset, en
  or or_1 (or_1_out, and_1_out, and_2_out);
  D_Flip_Flop d_ff_1 (.clk(clock_2_out), .D(or_1_out), .Q(d_ff_1_q), .Qn(d_ff_1_qn));  // open: preset, en, reset
  D_Flip_Flop d_ff_2 (.clk(clock_4_out), .D(in_2));  // open: Q, Qn, preset, en, reset
  Clock clock_5 (.out(clock_5_out));
  Clock clock_6 (.out(clock_6_out));
  not not_2 (not_2_out, D);
  J_K_Flip_Flop j_k_ff_1 (.J(D), .clk(clock_5_out), .K(not_2_out));  // open: Q, Qn, preset, en, reset
  Clock clock_7 (.out(clock_7_out));
  not not_3 (not_3_out, J_2);
  Clock clock_8 (.out(clock_8_out));
  and and_3 (and_3_out, t_ff_3_qn, J_2);
  or or_2 (or_2_out, K_2, not_3_out);
  J_K_Flip_Flop j_k_ff_2 (.J(in_3), .clk(clock_6_out), .K(in_5));  // open: Q, Qn, preset, en, reset
  xor xor_2 (xor_2_out, d_ff_3_q, T);
  D_Flip_Flop d_ff_3 (.clk(clock_8_out), .D(xor_2_out), .Q(d_ff_3_q));  // open: Qn, preset, en, reset
  and and_4 (and_4_out, or_2_out, t_ff_3_q);
  Clock clock_9 (.out(clock_9_out));
  or or_3 (or_3_out, and_3_out, and_4_out);
  S_R_Flip_Flop s_r_ff_1 (.S(in_4), .clk(clock_9_out), .R(in_6));  // open: Q, Qn, preset, reset, en
  T_Flip_Flop t_ff_3 (.clk(clock_7_out), .T(or_3_out), .Q(t_ff_3_q), .Qn(t_ff_3_qn));  // open: preset, reset, en

  // Notes on the sheet:
  //   Przerzutnik T
  //   Przerzutnik D za pomocą T
  //   Przerzutnik JK za pomocą D
  //   Przerzutnik D
  //   Przerzutnik D za pomocą JK
  //   Przerzutnik JK
  //   Przerzutnik JK za pomocą T
  //   Przerzutnik T za pomocą D
  //   Przerzutnik RS
endmodule
