// Logisim project T_1.circ as structural Verilog: 1 circuit, main circuit main
module main (
);

  wire and_1_out, and_2_out, clock_1_out, or_1_out, or_2_out, t_ff_1_q, t_ff_1_qn, t_ff_2_q, t_ff_3_q,
       t_ff_3_qn;

  Clock clock_1 (.out(clock_1_out));
  T_Flip_Flop t_ff_1 (.clk(clock_1_out), .T(t_ff_2_q), .Q(t_ff_1_q), .Qn(t_ff_1_qn));  // open: preset, reset, en
  or or_1 (or_1_out, t_ff_3_q, t_ff_2_q);
  T_Flip_Flop t_ff_2 (.clk(clock_1_out), .T(or_1_out), .Q(t_ff_2_q));  // open: Qn, preset, reset, en
  and and_1 (and_1_out, t_ff_1_q, t_ff_3_qn);
  T_Flip_Flop t_ff_3 (.clk(clock_1_out), .T(or_2_out), .Q(t_ff_3_q), .Qn(t_ff_3_qn));  // open: preset, reset, en
  and and_2 (and_2_out, t_ff_1_qn, t_ff_3_q);
  or or_2 (or_2_out, and_2_out, and_1_out);
endmodule
