// Logisim project Układ liczący 5-3-4-2-1 za pomocą JK.circ as structural Verilog: 1 circuit, main circuit main
module main (
  input  in_1,
  input  in_2,
  input  in_3,
  input  in_4,
  input  in_5,
  input  in_6
);

  wire and_1_out, clock_1_out, j_k_ff_1_q, j_k_ff_1_qn, j_k_ff_2_q, j_k_ff_3_q;

  and and_1 (and_1_out, j_k_ff_1_qn, j_k_ff_3_q);
  Clock clock_1 (.out(clock_1_out));
  J_K_Flip_Flop j_k_ff_1 (
    .J(and_1_out), .clk(clock_1_out), .K(1'b1), .Q(j_k_ff_1_q), .Qn(j_k_ff_1_qn), .preset(in_1), .reset(in_2));  // open: en
  J_K_Flip_Flop j_k_ff_2 (
    .J(j_k_ff_1_q), .clk(clock_1_out), .K(1'b1), .Q(j_k_ff_2_q), .preset(in_3), .reset(in_4));  // open: Qn, en
  J_K_Flip_Flop j_k_ff_3 (
    .J(j_k_ff_1_qn), .clk(clock_1_out), .K(j_k_ff_2_q), .Q(j_k_ff_3_q), .preset(in_5), .reset(in_6));  // open: Qn, en

  // Notes on the sheet:
  //   Ja = !Qa Qc
  //   Ka = 1
  //   Układ liczący 
  //   5->3->4->2->1
  //   za pomocą przerzutników JK
  //   Ctrl + K aby aktywować zegar
  //   Jb = Qa
  //   Kb = 1
  //   Jc = !Qa
  //   Kb = Qb
endmodule
