// Logisim project Zadanie 1 z zeszytu.circ as structural Verilog: 1 circuit, main circuit main
module main (
  input  Reset
);

  wire clock_1_out, j_k_ff_1_q, j_k_ff_1_qn, j_k_ff_2_qn, xor_1_out;

  xor xor_1 (xor_1_out, j_k_ff_1_q, j_k_ff_2_qn);
  Clock clock_1 (.out(clock_1_out));
  J_K_Flip_Flop j_k_ff_1 (
    .J(xor_1_out), .clk(clock_1_out), .K(1'b1), .Q(j_k_ff_1_q), .Qn(j_k_ff_1_qn), .reset(Reset));  // open: preset, en
  J_K_Flip_Flop j_k_ff_2 (
    .J(j_k_ff_1_qn), .clk(clock_1_out), .K(j_k_ff_1_q), .Qn(j_k_ff_2_qn), .reset(Reset));  // open: Q, preset, en

  // Notes on the sheet:
  //   Zadanie 1
  //   Wyznacz pełną trojektorię stanów poniższego układu + diagram stanów
endmodule
