// Logisim project circ1.circ as structural Verilog: 2 circuits, main circuit MyCircuit
module MyCircuit (
  input  x,
  input  y,
  input  z,
  input  We,
  output X_2,
  output Y_2,
  output Z_2,
  output Wy
);

  wire and_1_out, and_2_out, and_3_out, and_4_out, and_5_out, and_6_out, and_7_out, and_8_out, and_9_out,
       and_10_out, and_11_out, not_1_out, not_2_out, not_3_out, not_4_out, not_5_out, not_6_out, not_7_out,
       not_8_out, not_9_out, not_10_out, not_11_out, not_12_out, not_13_out;

  not not_1 (not_1_out, x);
  not not_2 (not_2_out, z);
  not not_3 (not_3_out, We);
  not not_4 (not_4_out, x);
  not not_5 (not_5_out, z);
  and and_1 (and_1_out, not_4_out, not_5_out, We);
  not not_6 (not_6_out, y);
  and and_2 (and_2_out, not_6_out, not_7_out, We);
  not not_7 (not_7_out, z);
  and and_3 (and_3_out, x, y, z, We);
  not not_8 (not_8_out, x);
  and and_4 (and_4_out, not_8_out, z, not_9_out);
  not not_9 (not_9_out, We);
  not not_10 (not_10_out, y);
  and and_5 (and_5_out, not_10_out, z, not_11_out);
  not not_11 (not_11_out, We);
  and and_6 (and_6_out, x, not_12_out, We);
  not not_12 (not_12_out, z);
  and and_7 (and_7_out, z, We);
  and and_8 (and_8_out, x, We);
  and and_9 (and_9_out, x, y, not_13_out);
  not not_13 (not_13_out, z);
  and and_10 (and_10_out, not_1_out, y, not_2_out, not_3_out);
  or or_1 (X_2, and_10_out, and_11_out);
  and and_11 (and_11_out, x, y, z, We);
  or or_2 (Y_2, and_1_out, and_2_out, and_3_out);
  or or_3 (Z_2, and_4_out, and_5_out, and_6_out);
  or or_4 (Wy, and_7_out, and_8_out, and_9_out);
endmodule

module Uklad_sekwencyjny (
  input  [6:0] in_1,
  output [6:0] out_2
);

  wire mycircuit_1_wy, mycircuit_1_y_2, mycircuit_2_wy, mycircuit_2_y_2, mycircuit_3_wy, mycircuit_3_y_2,
       mycircuit_4_wy, mycircuit_4_y_2, mycircuit_5_wy, mycircuit_5_y_2, mycircuit_6_wy, mycircuit_6_y_2,
       mycircuit_7_p3;

  MyCircuit mycircuit_1 (.y(1'b0), .We(1'b0), .Y_2(mycircuit_1_y_2), .Wy(mycircuit_1_wy));  // open: x, X_2, z, Z_2
  MyCircuit mycircuit_2 (
    .y(mycircuit_1_y_2), .We(mycircuit_1_wy), .Y_2(mycircuit_2_y_2), .Wy(mycircuit_2_wy));  // open: x, X_2, z, Z_2
  MyCircuit mycircuit_3 (
    .y(mycircuit_2_y_2), .We(mycircuit_2_wy), .Y_2(mycircuit_3_y_2), .Wy(mycircuit_3_wy));  // open: x, X_2, z, Z_2
  MyCircuit mycircuit_4 (
    .y(mycircuit_3_y_2), .We(mycircuit_3_wy), .Y_2(mycircuit_4_y_2), .Wy(mycircuit_4_wy));  // open: x, X_2, z, Z_2
  MyCircuit mycircuit_5 (
    .y(mycircuit_4_y_2), .We(mycircuit_4_wy), .Y_2(mycircuit_5_y_2), .Wy(mycircuit_5_wy));  // open: x, X_2, z, Z_2
  MyCircuit mycircuit_6 (
    .y(mycircuit_5_y_2), .We(mycircuit_5_wy), .Y_2(mycircuit_6_y_2), .Wy(mycircuit_6_wy));  // open: x, X_2, z, Z_2
  // MyCircuit mycircuit_7: pin names not known; wires that end beside it: mycircuit_6_y_2, mycircuit_6_wy, mycircuit_7_p3, in_1[0], 1'b0

  // Notes on the sheet:
  //   out_2: pull=up
endmodule
