// Logisim project mux4.circ as structural Verilog: 1 circuit, main circuit main
module main (
  input  A,
  input  B,
  input  C,
  input  D,
  output out_5
);

  wire not_1_out;

  not not_1 (not_1_out, D);
  Multiplexer #(.select(3)) multiplexer_1 (
    .in0(1'b1), .in1(D), .in2(not_1_out), .in3(1'b0), .in4(1'b1), .in5(1'b0), .in6(1'b0), .in7(D),
    .out(out_5), .sel({A, B, C}));  // open: en
endmodule
