// Logisim project mux5.circ as structural Verilog: 1 circuit, main circuit main
module main (
  input  A,
  input  B,
  input  C,
  input  D,
  output out_5
);

  wire multiplexer_1_out, multiplexer_2_out, multiplexer_3_out, multiplexer_4_out, not_1_out, not_2_out;

  not not_1 (not_1_out, D);
  not not_2 (not_2_out, D);
  Multiplexer multiplexer_1 (.in0(1'b1), .in1(not_1_out), .out(multiplexer_1_out), .sel(C));  // open: en
  Multiplexer multiplexer_2 (.in0(not_2_out), .in1(D), .out(multiplexer_2_out), .sel(C));  // open: en
  Multiplexer multiplexer_3 (.in0(1'b0), .in1(D), .out(multiplexer_3_out), .sel(C));  // open: en
  Multiplexer multiplexer_4 (.in0(1'b1), .in1(1'b0), .out(multiplexer_4_out), .sel(C));  // open: en
  Multiplexer #(.select(2)) multiplexer_5 (
    .in0(multiplexer_1_out), .in1(multiplexer_2_out), .in2(multiplexer_3_out), .in3(multiplexer_4_out),
    .out(out_5), .sel({A, B}));  // open: en
endmodule
