// Logisim project muxGlosowanie.circ as structural Verilog: 1 circuit, main circuit main
module main (
  input  A,
  input  B,
  input  C,
  output out_4
);

  Multiplexer #(.select(2)) multiplexer_1 (
    .in0(1'b0), .in1(C), .in2(C), .in3(1'b1), .out(out_4), .sel({A, B}));  // open: en
endmodule
