// Logisim project negujNa01zPrawejInORAZnieparz1Zlewej.circ as structural Verilog: 2 circuits, main circuit main
module main (
  input  [7:0] in_1,
  output [7:0] out_2
);

  wire iter1_1_p_2, iter1_2_a_2, iter1_2_b_2, iter1_2_p_2, iter1_3_a_2, iter1_3_b_2, iter1_3_p_2,
       iter1_4_a_2, iter1_4_b_2, iter1_4_p_2, iter1_5_a_2, iter1_5_b_2, iter1_5_p_2, iter1_6_a_2,
       iter1_6_b_2, iter1_6_p_2, iter1_7_a_2, iter1_7_b_2, iter1_7_p_2, iter1_8_a_2, iter1_8_b_2;

  iter1 iter1_1 (
    .We(in_1[7]), .Wy(out_2[7]), .p(1'b0), .a(iter1_2_a_2), .P_2(iter1_1_p_2), .b(iter1_2_b_2));  // open: A_2, B_2
  iter1 iter1_2 (
    .We(in_1[6]), .Wy(out_2[6]), .p(iter1_1_p_2), .a(iter1_3_a_2), .P_2(iter1_2_p_2), .b(iter1_3_b_2),
    .A_2(iter1_2_a_2), .B_2(iter1_2_b_2));
  iter1 iter1_3 (
    .We(in_1[5]), .Wy(out_2[5]), .p(iter1_2_p_2), .a(iter1_4_a_2), .P_2(iter1_3_p_2), .b(iter1_4_b_2),
    .A_2(iter1_3_a_2), .B_2(iter1_3_b_2));
  iter1 iter1_4 (
    .We(in_1[4]), .Wy(out_2[4]), .p(iter1_3_p_2), .a(iter1_5_a_2), .P_2(iter1_4_p_2), .b(iter1_5_b_2),
    .A_2(iter1_4_a_2), .B_2(iter1_4_b_2));
  iter1 iter1_5 (
    .We(in_1[3]), .Wy(out_2[3]), .p(iter1_4_p_2), .a(iter1_6_a_2), .P_2(iter1_5_p_2), .b(iter1_6_b_2),
    .A_2(iter1_5_a_2), .B_2(iter1_5_b_2));
  iter1 iter1_6 (
    .We(in_1[2]), .Wy(out_2[2]), .p(iter1_5_p_2), .a(iter1_7_a_2), .P_2(iter1_6_p_2), .b(iter1_7_b_2),
    .A_2(iter1_6_a_2), .B_2(iter1_6_b_2));
  iter1 iter1_7 (
    .We(in_1[1]), .Wy(out_2[1]), .p(iter1_6_p_2), .a(iter1_8_a_2), .P_2(iter1_7_p_2), .b(iter1_8_b_2),
    .A_2(iter1_7_a_2), .B_2(iter1_7_b_2));
  iter1 iter1_8 (
    .We(in_1[0]), .Wy(out_2[0]), .p(iter1_7_p_2), .a(1'b0), .b(1'b0), .A_2(iter1_8_a_2), .B_2(iter1_8_b_2));  // open: P_2
endmodule

module iter1 (
  input  We,
  input  p,
  input  a,
  input  b,
  output Wy,
  output P_2,
  output A_2,
  output B_2
);

  wire and_1_out, and_2_out, not_1_out, not_2_out, not_3_out, not_4_out, not_5_out;

  not not_1 (not_1_out, b);
  not not_2 (not_2_out, We);
  and and_1 (and_1_out, p, not_3_out);
  not not_3 (not_3_out, We);
  not not_4 (not_4_out, p);
  and and_2 (and_2_out, not_4_out, We);
  not not_5 (not_5_out, We);
  and and_3 (A_2, not_5_out, b);
  and and_4 (Wy, p, a, not_1_out, not_2_out);
  or or_1 (P_2, and_1_out, and_2_out);

  assign B_2 = We;
endmodule
