// Logisim project przepisz3jedynki.circ as structural Verilog: 2 circuits, main circuit main
module main (
  input  [5:0] in_1,
  output [5:0] out_2
);

  wire ukladmy_1_a_2, ukladmy_1_b_2, ukladmy_2_a_2, ukladmy_2_b_2, ukladmy_2_p_2, ukladmy_3_a_2,
       ukladmy_3_b_2, ukladmy_3_p_2, ukladmy_4_a_2, ukladmy_4_b_2, ukladmy_4_p_2, ukladmy_5_a_2,
       ukladmy_5_b_2, ukladmy_5_p_2, ukladmy_6_p_2;

  ukladMy ukladmy_1 (
    .a(1'b0), .A_2(ukladmy_1_a_2), .b(1'b0), .x(in_1[5]), .B_2(ukladmy_1_b_2), .p(ukladmy_2_p_2), .Y(out_2[5]));  // open: P_2
  ukladMy ukladmy_2 (
    .a(ukladmy_1_a_2), .A_2(ukladmy_2_a_2), .b(ukladmy_1_b_2), .x(in_1[4]), .B_2(ukladmy_2_b_2),
    .p(ukladmy_3_p_2), .Y(out_2[4]), .P_2(ukladmy_2_p_2));
  ukladMy ukladmy_3 (
    .a(ukladmy_2_a_2), .A_2(ukladmy_3_a_2), .b(ukladmy_2_b_2), .x(in_1[3]), .B_2(ukladmy_3_b_2),
    .p(ukladmy_4_p_2), .Y(out_2[3]), .P_2(ukladmy_3_p_2));
  ukladMy ukladmy_4 (
    .a(ukladmy_3_a_2), .A_2(ukladmy_4_a_2), .b(ukladmy_3_b_2), .x(in_1[2]), .B_2(ukladmy_4_b_2),
    .p(ukladmy_5_p_2), .Y(out_2[2]), .P_2(ukladmy_4_p_2));
  ukladMy ukladmy_5 (
    .a(ukladmy_4_a_2), .A_2(ukladmy_5_a_2), .b(ukladmy_4_b_2), .x(in_1[1]), .B_2(ukladmy_5_b_2),
    .p(ukladmy_6_p_2), .Y(out_2[1]), .P_2(ukladmy_5_p_2));
  ukladMy ukladmy_6 (
    .a(ukladmy_5_a_2), .b(ukladmy_5_b_2), .x(in_1[0]), .p(1'b0), .Y(out_2[0]), .P_2(ukladmy_6_p_2));  // open: A_2, B_2
endmodule

module ukladMy (
  input  a,
  input  b,
  input  x,
  input  p,
  output A_2,
  output B_2,
  output Y,
  output P_2
);

  wire and_1_out, and_2_out, and_3_out, and_4_out, and_5_out, and_6_out, and_7_out, and_8_out, not_1_out;

  and and_1 (and_1_out, b, x);
  and and_2 (and_2_out, a, x);
  not not_1 (not_1_out, b);
  and and_3 (and_3_out, not_1_out, x);
  and and_4 (and_4_out, a, x);
  and and_5 (and_5_out, a, x);
  and and_6 (and_6_out, p, x);
  and and_7 (and_7_out, a, x);
  and and_8 (and_8_out, x, p);
  or or_1 (A_2, and_1_out, and_2_out);
  or or_2 (B_2, and_3_out, and_4_out);
  or or_3 (Y, and_5_out, and_6_out);
  or or_4 (P_2, and_7_out, and_8_out);
endmodule
