// Logisim project uklad1.circ as structural Verilog: 2 circuits, main circuit main
module main (
  input  [5:0] in_1,
  output [5:0] out_2
);

  wire subcircuit1_1_a_2, subcircuit1_1_b_2, subcircuit1_2_a_2, subcircuit1_2_b_2, subcircuit1_2_p_2,
       subcircuit1_3_a_2, subcircuit1_3_b_2, subcircuit1_3_p_2, subcircuit1_4_a_2, subcircuit1_4_b_2,
       subcircuit1_4_p_2, subcircuit1_5_a_2, subcircuit1_5_b_2, subcircuit1_5_p_2, subcircuit1_6_p_2;

  subcircuit1 subcircuit1_1 (
    .a(1'b0), .b(1'b0), .x(in_1[5]), .p(subcircuit1_2_p_2), .A_2(subcircuit1_1_a_2), .B_2(subcircuit1_1_b_2),
    .Y(out_2[5]));  // open: P_2
  subcircuit1 subcircuit1_2 (
    .a(subcircuit1_1_a_2), .b(subcircuit1_1_b_2), .x(in_1[4]), .p(subcircuit1_3_p_2),
    .A_2(subcircuit1_2_a_2), .B_2(subcircuit1_2_b_2), .Y(out_2[4]), .P_2(subcircuit1_2_p_2));
  subcircuit1 subcircuit1_3 (
    .a(subcircuit1_2_a_2), .b(subcircuit1_2_b_2), .x(in_1[3]), .p(subcircuit1_4_p_2),
    .A_2(subcircuit1_3_a_2), .B_2(subcircuit1_3_b_2), .Y(out_2[3]), .P_2(subcircuit1_3_p_2));
  subcircuit1 subcircuit1_4 (
    .a(subcircuit1_3_a_2), .b(subcircuit1_3_b_2), .x(in_1[2]), .p(subcircuit1_5_p_2),
    .A_2(subcircuit1_4_a_2), .B_2(subcircuit1_4_b_2), .Y(out_2[2]), .P_2(subcircuit1_4_p_2));
  subcircuit1 subcircuit1_5 (
    .a(subcircuit1_4_a_2), .b(subcircuit1_4_b_2), .x(in_1[1]), .p(subcircuit1_6_p_2),
    .A_2(subcircuit1_5_a_2), .B_2(subcircuit1_5_b_2), .Y(out_2[1]), .P_2(subcircuit1_5_p_2));
  subcircuit1 subcircuit1_6 (
    .a(subcircuit1_5_a_2), .b(subcircuit1_5_b_2), .x(in_1[0]), .p(1'b0), .Y(out_2[0]), .P_2(subcircuit1_6_p_2));  // open: A_2, B_2
endmodule

module subcircuit1 (
  input  a,
  input  b,
  input  x,
  input  p,
  output A_2,
  output B_2,
  output Y,
  output P_2
);

  wire and_1_out, and_2_out, and_3_out, and_4_out, and_5_out, and_6_out, and_7_out, and_8_out, and_9_out,
       and_10_out, and_11_out, and_12_out, not_1_out, not_2_out, not_3_out, not_4_out, not_5_out;

  not not_1 (not_1_out, b);
  and and_1 (and_1_out, not_1_out, x);
  and and_2 (and_2_out, a, x);
  and and_3 (and_3_out, x, p);
  and and_4 (and_4_out, a, x);
  and and_5 (and_5_out, b, x, p);
  and and_6 (and_6_out, a, x);
  and and_7 (and_7_out, a, b);
  and and_8 (and_8_out, b, not_2_out, p);
  not not_2 (not_2_out, x);
  and and_9 (and_9_out, b, x, not_3_out);
  not not_3 (not_3_out, p);
  not not_4 (not_4_out, x);
  and and_10 (and_10_out, a, not_4_out, p);
  and and_11 (and_11_out, a, x, not_5_out);
  not not_5 (not_5_out, p);
  and and_12 (and_12_out, a, b, x);
  or or_1 (A_2, and_1_out, and_2_out);
  or or_2 (B_2, and_3_out, and_4_out);
  or or_3 (Y, and_5_out, and_6_out, and_7_out);
  or or_4 (P_2, and_8_out, and_9_out, and_10_out, and_11_out, and_12_out);
endmodule
