// Logisim project zadanie 1.circ as structural Verilog: 2 circuits, main circuit main
module main (
  input  [6:0] in_1,
  output [6:0] out_2
);

  wire uklad1_1_x_2, uklad1_1_y_2, uklad1_2_v_2, uklad1_2_x_2, uklad1_2_y_2, uklad1_3_v_2, uklad1_3_x_2,
       uklad1_3_y_2, uklad1_4_v_2, uklad1_4_x_2, uklad1_4_y_2, uklad1_5_v_2, uklad1_5_x_2, uklad1_5_y_2,
       uklad1_6_v_2, uklad1_6_x_2, uklad1_6_y_2, uklad1_7_v_2;

  Uklad1 uklad1_1 (
    .x(1'b0), .y(1'b0), .v(uklad1_2_v_2), .a(in_1[6]), .X_2(uklad1_1_x_2), .Y_2(uklad1_1_y_2), .Z(out_2[6]));  // open: V_2
  Uklad1 uklad1_2 (
    .x(uklad1_1_x_2), .y(uklad1_1_y_2), .v(uklad1_3_v_2), .a(in_1[5]), .X_2(uklad1_2_x_2),
    .Y_2(uklad1_2_y_2), .V_2(uklad1_2_v_2), .Z(out_2[5]));
  Uklad1 uklad1_3 (
    .x(uklad1_2_x_2), .y(uklad1_2_y_2), .v(uklad1_4_v_2), .a(in_1[4]), .X_2(uklad1_3_x_2),
    .Y_2(uklad1_3_y_2), .V_2(uklad1_3_v_2), .Z(out_2[4]));
  Uklad1 uklad1_4 (
    .x(uklad1_3_x_2), .y(uklad1_3_y_2), .v(uklad1_5_v_2), .a(in_1[3]), .X_2(uklad1_4_x_2),
    .Y_2(uklad1_4_y_2), .V_2(uklad1_4_v_2), .Z(out_2[3]));
  Uklad1 uklad1_5 (
    .x(uklad1_4_x_2), .y(uklad1_4_y_2), .v(uklad1_6_v_2), .a(in_1[2]), .X_2(uklad1_5_x_2),
    .Y_2(uklad1_5_y_2), .V_2(uklad1_5_v_2), .Z(out_2[2]));
  Uklad1 uklad1_6 (
    .x(uklad1_5_x_2), .y(uklad1_5_y_2), .v(uklad1_7_v_2), .a(in_1[1]), .X_2(uklad1_6_x_2),
    .Y_2(uklad1_6_y_2), .V_2(uklad1_6_v_2), .Z(out_2[1]));
  Uklad1 uklad1_7 (
    .x(uklad1_6_x_2), .y(uklad1_6_y_2), .v(1'b0), .a(in_1[0]), .V_2(uklad1_7_v_2), .Z(out_2[0]));  // open: X_2, Y_2
endmodule

module Uklad1 (
  input  x,
  input  y,
  input  v,
  input  a,
  output X_2,
  output Y_2,
  output V_2,
  output Z
);

  wire and_1_out, and_2_out, and_3_out, and_4_out, and_5_out, and_6_out, not_1_out, not_2_out, not_3_out,
       not_4_out, not_5_out;

  and and_1 (and_1_out, y, a);
  not not_1 (not_1_out, x);
  not not_2 (not_2_out, y);
  not not_3 (not_3_out, a);
  and and_2 (and_2_out, x, a);
  not not_4 (not_4_out, x);
  not not_5 (not_5_out, v);
  or or_1 (X_2, and_1_out, x);
  and and_3 (and_3_out, not_1_out, not_2_out, a);
  and and_4 (and_4_out, y, not_3_out);
  or or_2 (V_2, v, and_2_out);
  and and_5 (and_5_out, not_4_out, a);
  and and_6 (and_6_out, not_5_out, a);
  or or_3 (Y_2, and_3_out, and_4_out);
  or or_4 (Z, and_5_out, and_6_out);
endmodule
