// Logisim project zadanie 12.circ as structural Verilog: 2 circuits, main circuit main
module main (
  input  [7:0] in_1,
  output [7:0] out_2
);

  wire zerownik_1_x_2, zerownik_1_y_2, zerownik_2_x_2, zerownik_2_y_2, zerownik_2_z_2, zerownik_3_x_2,
       zerownik_3_y_2, zerownik_3_z_2, zerownik_4_x_2, zerownik_4_y_2, zerownik_4_z_2, zerownik_5_x_2,
       zerownik_5_y_2, zerownik_5_z_2, zerownik_6_x_2, zerownik_6_y_2, zerownik_6_z_2, zerownik_7_x_2,
       zerownik_7_z_2, zerownik_8_z_2;

  Zerownik zerownik_1 (
    .x(1'b0), .X_2(zerownik_1_x_2), .y(1'b0), .z(zerownik_2_z_2), .Y_2(zerownik_1_y_2), .We(in_1[7]),
    .Wy(out_2[7]));  // open: Z_2
  Zerownik zerownik_2 (
    .x(zerownik_1_x_2), .X_2(zerownik_2_x_2), .y(zerownik_1_y_2), .z(zerownik_3_z_2), .Y_2(zerownik_2_y_2),
    .We(in_1[6]), .Z_2(zerownik_2_z_2), .Wy(out_2[6]));
  Zerownik zerownik_3 (
    .x(zerownik_2_x_2), .X_2(zerownik_3_x_2), .y(zerownik_2_y_2), .z(zerownik_4_z_2), .Y_2(zerownik_3_y_2),
    .We(in_1[5]), .Z_2(zerownik_3_z_2), .Wy(out_2[5]));
  Zerownik zerownik_4 (
    .x(zerownik_3_x_2), .X_2(zerownik_4_x_2), .y(zerownik_3_y_2), .z(zerownik_5_z_2), .Y_2(zerownik_4_y_2),
    .We(in_1[4]), .Z_2(zerownik_4_z_2), .Wy(out_2[4]));
  Zerownik zerownik_5 (
    .x(zerownik_4_x_2), .X_2(zerownik_5_x_2), .y(zerownik_4_y_2), .z(zerownik_6_z_2), .Y_2(zerownik_5_y_2),
    .We(in_1[3]), .Z_2(zerownik_5_z_2), .Wy(out_2[3]));
  Zerownik zerownik_6 (
    .x(zerownik_5_x_2), .X_2(zerownik_6_x_2), .y(zerownik_5_y_2), .z(zerownik_7_z_2), .Y_2(zerownik_6_y_2),
    .We(in_1[2]), .Z_2(zerownik_6_z_2), .Wy(out_2[2]));
  Zerownik zerownik_7 (
    .x(zerownik_6_x_2), .X_2(zerownik_7_x_2), .y(zerownik_6_y_2), .z(zerownik_8_z_2), .Y_2(zerownik_7_x_2),
    .We(in_1[1]), .Z_2(zerownik_7_z_2), .Wy(out_2[1]));
  Zerownik zerownik_8 (
    .x(zerownik_7_x_2), .y(zerownik_7_x_2), .z(1'b0), .We(in_1[0]), .Z_2(zerownik_8_z_2), .Wy(out_2[0]));  // open: X_2, Y_2

  // Notes on the sheet:
  //   in_1: pull=up
  //   xy
  //   z - komenda "zeruj" (wysyłana w lewo)
  //   00 - nie znaleziono niczego
  //   01 - znaleziono pierwszy bit
  //   10 - znaleziono pierwszy i drugi bit
  //   11 - komenda "zeruj" (wysyłana w prawo)
endmodule

module Zerownik (
  input  x,
  input  y,
  input  z,
  input  We,
  output X_2,
  output Y_2,
  output Z_2,
  output Wy
);

  wire and_1_out, and_2_out, and_3_out, and_4_out, and_5_out, and_6_out, and_7_out, and_8_out, not_1_out,
       not_2_out, not_3_out, not_4_out, not_5_out, not_6_out, not_7_out, not_8_out;

  and and_1 (and_1_out, y, We);
  not not_1 (not_1_out, x);
  and and_2 (and_2_out, not_1_out, not_2_out, We);
  not not_2 (not_2_out, y);
  and and_3 (and_3_out, x, not_3_out);
  not not_3 (not_3_out, We);
  and and_4 (and_4_out, x, y);
  and and_5 (and_5_out, x, not_4_out);
  not not_4 (not_4_out, We);
  and and_6 (and_6_out, x, y);
  not not_5 (not_5_out, x);
  not not_6 (not_6_out, z);
  and and_7 (and_7_out, not_5_out, not_6_out, We);
  not not_7 (not_7_out, y);
  and and_8 (and_8_out, not_7_out, not_8_out, We);
  not not_8 (not_8_out, z);
  or or_1 (X_2, and_1_out, x);
  or or_2 (Y_2, and_2_out, and_3_out, and_4_out);
  or or_3 (Z_2, z, and_5_out, and_6_out);
  or or_4 (Wy, and_7_out, and_8_out);
endmodule
