// Logisim project zadanie 9.circ as structural Verilog: 2 circuits, main circuit main
module main (
  input  [7:0] in_1,
  output [7:0] out_2
);

  wire uklad01np_1_p_2, uklad01np_2_p_2, uklad01np_2_x_2, uklad01np_2_y_2, uklad01np_3_p_2, uklad01np_3_x_2,
       uklad01np_3_y_2, uklad01np_4_p_2, uklad01np_4_x_2, uklad01np_4_y_2, uklad01np_5_p_2, uklad01np_5_x_2,
       uklad01np_5_y_2, uklad01np_6_p_2, uklad01np_6_x_2, uklad01np_6_y_2, uklad01np_7_p_2, uklad01np_7_x_2,
       uklad01np_7_y_2, uklad01np_8_x_2, uklad01np_8_y_2;

  Uklad01Np uklad01np_1 (
    .x(uklad01np_2_x_2), .y(uklad01np_2_y_2), .p(1'b0), .We(in_1[7]), .P_2(uklad01np_1_p_2), .Wy(out_2[7]));  // open: X_2, Y_2
  Uklad01Np uklad01np_2 (
    .x(uklad01np_3_x_2), .X_2(uklad01np_2_x_2), .y(uklad01np_3_y_2), .p(uklad01np_1_p_2),
    .Y_2(uklad01np_2_y_2), .We(in_1[6]), .P_2(uklad01np_2_p_2), .Wy(out_2[6]));
  Uklad01Np uklad01np_3 (
    .x(uklad01np_4_x_2), .X_2(uklad01np_3_x_2), .y(uklad01np_4_y_2), .p(uklad01np_2_p_2),
    .Y_2(uklad01np_3_y_2), .We(in_1[5]), .P_2(uklad01np_3_p_2), .Wy(out_2[5]));
  Uklad01Np uklad01np_4 (
    .x(uklad01np_5_x_2), .X_2(uklad01np_4_x_2), .y(uklad01np_5_y_2), .p(uklad01np_3_p_2),
    .Y_2(uklad01np_4_y_2), .We(in_1[4]), .P_2(uklad01np_4_p_2), .Wy(out_2[4]));
  Uklad01Np uklad01np_5 (
    .x(uklad01np_6_x_2), .X_2(uklad01np_5_x_2), .y(uklad01np_6_y_2), .p(uklad01np_4_p_2),
    .Y_2(uklad01np_5_y_2), .We(in_1[3]), .P_2(uklad01np_5_p_2), .Wy(out_2[3]));
  Uklad01Np uklad01np_6 (
    .x(uklad01np_7_x_2), .X_2(uklad01np_6_x_2), .y(uklad01np_7_y_2), .p(uklad01np_5_p_2),
    .Y_2(uklad01np_6_y_2), .We(in_1[2]), .P_2(uklad01np_6_p_2), .Wy(out_2[2]));
  Uklad01Np uklad01np_7 (
    .x(uklad01np_8_x_2), .X_2(uklad01np_7_x_2), .y(uklad01np_8_y_2), .p(uklad01np_6_p_2),
    .Y_2(uklad01np_7_y_2), .We(in_1[1]), .P_2(uklad01np_7_p_2), .Wy(out_2[1]));
  Uklad01Np uklad01np_8 (
    .x(1'b0), .X_2(uklad01np_8_x_2), .y(1'b0), .p(uklad01np_7_p_2), .Y_2(uklad01np_8_y_2), .We(in_1[0]),
    .Wy(out_2[0]));  // open: P_2
endmodule

module Uklad01Np (
  input  x,
  input  y,
  input  p,
  input  We,
  output X_2,
  output Y_2,
  output P_2,
  output Wy
);

  wire and_2_out, and_3_out, and_4_out, and_5_out, and_6_out, and_7_out, and_8_out, and_9_out, and_10_out,
       not_1_out, not_2_out, not_3_out, not_4_out, not_5_out, not_6_out, not_7_out, not_8_out, not_9_out,
       not_10_out, not_11_out;

  and and_1 (X_2, y, not_1_out);
  not not_1 (not_1_out, We);
  not not_2 (not_2_out, x);
  and and_2 (and_2_out, not_2_out, We);
  not not_3 (not_3_out, p);
  and and_3 (and_3_out, not_3_out, We);
  and and_4 (and_4_out, y, We);
  not not_4 (not_4_out, x);
  and and_5 (and_5_out, not_4_out, not_5_out, We);
  not not_5 (not_5_out, p);
  not not_6 (not_6_out, y);
  not not_7 (not_7_out, p);
  and and_6 (and_6_out, not_6_out, not_7_out, We);
  and and_7 (and_7_out, p, not_8_out);
  not not_8 (not_8_out, We);
  not not_9 (not_9_out, x);
  and and_8 (and_8_out, not_9_out, We);
  not not_10 (not_10_out, p);
  and and_9 (and_9_out, not_10_out, We);
  and and_10 (and_10_out, x, p, not_11_out);
  not not_11 (not_11_out, We);
  or or_1 (Y_2, and_2_out, and_3_out, and_4_out);
  or or_2 (P_2, and_5_out, and_6_out, and_7_out);
  or or_3 (Wy, and_8_out, and_9_out, and_10_out);
endmodule
