// Logisim project zerujNa110.circ as structural Verilog: 2 circuits, main circuit main
module main (
  input  [7:0] in_1,
  output [7:0] out_2
);

  wire zerujna110_1_x_2, zerujna110_1_y_2, zerujna110_2_x_2, zerujna110_2_y_2, zerujna110_2_z_2,
       zerujna110_3_x_2, zerujna110_3_y_2, zerujna110_3_z_2, zerujna110_4_x_2, zerujna110_4_y_2,
       zerujna110_4_z_2, zerujna110_5_x_2, zerujna110_5_y_2, zerujna110_5_z_2, zerujna110_6_x_2,
       zerujna110_6_y_2, zerujna110_6_z_2, zerujna110_7_x_2, zerujna110_7_y_2, zerujna110_7_z_2,
       zerujna110_8_z_2;

  zerujNa110 zerujna110_1 (
    .x(1'b0), .y(1'b0), .We(in_1[7]), .z(zerujna110_2_z_2), .X_2(zerujna110_1_x_2), .Y_2(zerujna110_1_y_2),
    .Wy(out_2[7]));  // open: Z_2
  zerujNa110 zerujna110_2 (
    .x(zerujna110_1_x_2), .y(zerujna110_1_y_2), .We(in_1[6]), .z(zerujna110_3_z_2), .X_2(zerujna110_2_x_2),
    .Y_2(zerujna110_2_y_2), .Wy(out_2[6]), .Z_2(zerujna110_2_z_2));
  zerujNa110 zerujna110_3 (
    .x(zerujna110_2_x_2), .y(zerujna110_2_y_2), .We(in_1[5]), .z(zerujna110_4_z_2), .X_2(zerujna110_3_x_2),
    .Y_2(zerujna110_3_y_2), .Wy(out_2[5]), .Z_2(zerujna110_3_z_2));
  zerujNa110 zerujna110_4 (
    .x(zerujna110_3_x_2), .y(zerujna110_3_y_2), .We(in_1[4]), .z(zerujna110_6_z_2), .X_2(zerujna110_4_x_2),
    .Y_2(zerujna110_4_y_2), .Wy(out_2[4]), .Z_2(zerujna110_4_z_2));
  zerujNa110 zerujna110_5 (
    .x(zerujna110_6_x_2), .y(zerujna110_6_y_2), .We(in_1[2]), .z(zerujna110_7_z_2), .X_2(zerujna110_5_x_2),
    .Y_2(zerujna110_5_y_2), .Wy(out_2[2]), .Z_2(zerujna110_5_z_2));
  zerujNa110 zerujna110_6 (
    .x(zerujna110_4_x_2), .y(zerujna110_4_y_2), .We(in_1[3]), .z(zerujna110_5_z_2), .X_2(zerujna110_6_x_2),
    .Y_2(zerujna110_6_y_2), .Wy(out_2[3]), .Z_2(zerujna110_6_z_2));
  zerujNa110 zerujna110_7 (
    .x(zerujna110_5_x_2), .y(zerujna110_5_y_2), .We(in_1[1]), .z(zerujna110_8_z_2), .X_2(zerujna110_7_x_2),
    .Y_2(zerujna110_7_y_2), .Wy(out_2[1]), .Z_2(zerujna110_7_z_2));
  zerujNa110 zerujna110_8 (
    .x(zerujna110_7_x_2), .y(zerujna110_7_y_2), .We(in_1[0]), .z(1'b0), .Wy(out_2[0]), .Z_2(zerujna110_8_z_2));  // open: X_2, Y_2

  // Notes on the sheet:
  //   Zeruj po wykryciu 110
endmodule

module zerujNa110 (
  input  x,
  input  y,
  input  We,
  input  z,
  output X_2,
  output Y_2,
  output Wy,
  output Z_2
);

  wire and_1_out, and_2_out, and_3_out, and_4_out, and_5_out, and_6_out, and_7_out, not_1_out, not_2_out,
       not_3_out, not_4_out, not_5_out, not_6_out, not_7_out, not_8_out, not_9_out;

  and and_1 (and_1_out, y, We);
  not not_1 (not_1_out, x);
  not not_2 (not_2_out, y);
  and and_2 (and_2_out, not_1_out, not_2_out, We);
  and and_3 (and_3_out, x, not_3_out);
  not not_3 (not_3_out, We);
  and and_4 (and_4_out, x, y);
  not not_4 (not_4_out, x);
  and and_5 (and_5_out, not_4_out, We, not_5_out);
  not not_5 (not_5_out, z);
  not not_6 (not_6_out, y);
  and and_6 (and_6_out, not_6_out, We, not_7_out);
  not not_7 (not_7_out, z);
  and and_7 (and_7_out, x, not_8_out, not_9_out);
  not not_8 (not_8_out, y);
  not not_9 (not_9_out, We);
  or or_1 (X_2, and_1_out, x);
  or or_2 (Y_2, and_2_out, and_3_out, and_4_out);
  or or_3 (Wy, and_5_out, and_6_out);
  or or_4 (Z_2, and_7_out, z);
endmodule
